# Fritzing sketch making board (saved by Fritzing 0.9.3b)
circuit board: 8.46667cm x 5.64444cm
breadboards: 1

parts:
  Part2 = 9-DOF Absolute Orientation IMU Fusion Breakout - BNO055
  R1 = Resistor [tolerance=±5% resistance=1M package=THT]
  Part3 = Arduino Uno (Rev3)
  R2 = Resistor [tolerance=±5% resistance=1M package=THT]
  J1 = female pin header, 1 pin [form="♀ (female)"]
  J2 = female pin header, 1 pin [form="♀ (female)"]
  J3 = female pin header, 2 pins [form="♀ (female)"]
  R3 = Resistor [tolerance=±5% resistance=100 package=THT]
  R4 = Resistor [tolerance=±5% resistance=100 package=THT]
  R5 = Resistor [tolerance=±5% resistance=100 package=THT]
  J4 = female pin header, 2 pins [form="♀ (female)"]
  J5 = female pin header, 2 pins [form="♀ (female)"]
  J6 = Piezo Speaker

nets (from the pcb view):
  N1: Part2.5.0V, Part3.5V
  GND: Part2.GND, Part3.GND, J3.pin2, J4.pin2, J5.pin2, J6.pin1
  N2: Part2.SDA_5V, Part3.A4/SDA
  N3: Part2.SCL_5V, Part3.A5/SCL
  N4: R1.Pin_0, Part3.D4, J2.pin1
  N5: R1.Pin_1, Part3.D5_PWM
  N6: Part3.A0, J6.pin2
  N7: Part3.D8, R5.Pin_1
  N8: Part3.D2, R2.Pin_0, J1.pin1
  N9: Part3.D3_PWM, R2.Pin_1
  N10: Part3.D6_PWM, R4.Pin_1
  N11: Part3.D7, R3.Pin_1
  N12: J3.pin1, R4.Pin_0, R5.Pin_0, J4.pin1
  N13: R3.Pin_0, J5.pin1

custom parts:
  9-DOF Absolute Orientation IMU Fusion Breakout - BNO055: A MEMS accelerometer, magnetometer and gyroscope on a single die with a high speed ARM Cortex-M0 based processor to digest all the sensor data, abstract the sensor fusion and real time requirements away, and spit out data you can use in quaternions, Euler angles or vectors.
